# Fritzing sketch P2Platest (saved by Fritzing 0.9.5d)
breadboards: 1

parts:
  Part3 = Power Cell LiPo Charger/Booster
  Part4 = NRF24L01
  U1 = SWITCH_SPDT [package=kps-1290]
  C1 = Capacitor Polarized [package=cpol-radial-10uf-25v]
  S2 = Pushbutton [package="[SMD]"]
  S3 = Pushbutton [package="[SMD]"]
  S4 = Pushbutton [package="[SMD]"]
  LED1 = smd LED [color="Red (633nm)" package="0805 [SMD]"]
  LED2 = smd LED [color="Yellow (595nm)" package="0805 [SMD]"]
  LED3 = smd LED [color="Green (555nm)" package="0805 [SMD]"]
  R1 = Resistor [tolerance=±1% resistance=330 package="0603 [SMD]"]
  R2 = Resistor [tolerance=±1% resistance=330 package="0603 [SMD]"]
  R3 = Resistor [tolerance=±1% resistance=330 package="0603 [SMD]"]
  VCC1 = 4 x AAA Battery Mount
  0 = Arduino Nano (Rev3.0)

nets:
  N1: Part3.VCC, U1.S
  GND: Part3.GND, S2.Pin_3, S2.Pin_4, S3.Pin_3, S3.Pin_4, S4.Pin_3, S4.Pin_4, VCC1.-, 0.GND
  N2: Part3.5VIN, R1.Pin_0, R2.Pin_0, R3.Pin_0, 0.5V
  N3: Part4.MOSI, 0.D11/MOSI
  N4: Part4.CSN, 0.D10
  VCC: Part4.VCC, C1.+, 0.3V3
  N5: Part4.MISO, 0.D12/MISO
  N6: Part4.SCK, 0.D13/SCK
  N7: Part4.CE, 0.D9
  N8: Part4.GND, C1.-
  N9: U1.P, VCC1.+
  N10: S2.Pin_1, S2.Pin_2, 0.D2
  N11: S3.Pin_1, S3.Pin_2, 0.D3
  N12: S4.Pin_1, S4.Pin_2, 0.D4
  N13: LED1.cathode, 0.D7
  N14: LED1.anode, R1.Pin_1
  N15: LED2.cathode, 0.D6
  N16: LED2.anode, R2.Pin_1
  N17: LED3.cathode, 0.D5
  N18: LED3.anode, R3.Pin_1
