# Fritzing sketch P2Platest (saved by Fritzing 0.9.5d)
breadboards: 1

parts:
  Part3 = Power Cell LiPo Charger/Booster
  U1 = SWITCH_SPDT [package=kps-1290]
  C1 = Capacitor Polarized [package=cpol-radial-10uf-25v]
  S2 = Pushbutton [package="[SMD]"]
  S3 = Pushbutton [package="[SMD]"]
  S4 = Pushbutton [package="[SMD]"]
  LED1 = smd LED [color="Red (633nm)" package="0805 [SMD]"]
  LED2 = smd LED [color="Yellow (595nm)" package="0805 [SMD]"]
  LED3 = smd LED [color="Green (555nm)" package="0805 [SMD]"]
  R1 = Resistor [tolerance=±1% resistance=330 package="0603 [SMD]"]
  R2 = Resistor [tolerance=±1% resistance=330 package="0603 [SMD]"]
  R3 = Resistor [tolerance=±1% resistance=330 package="0603 [SMD]"]
  0 = Arduino Nano (Rev3.0)
  BAT1 = 18650 battery holder [package=battery-18650-kit]
  Part5 = NRF24L01+ Breakout Board

nets:
  VCC: Part3.VCC, R1.Pin_0, R2.Pin_0, R3.Pin_0, 0.5V
  GND: Part3.GND, S2.Pin_3, S2.Pin_4, S3.Pin_3, S3.Pin_4, S4.Pin_3, S4.Pin_4, 0.GND, BAT1.-
  N1: Part3.5VIN, U1.S
  N2: U1.P, BAT1.+
  3V3: C1.+, 0.3V3, Part5.VCC
  N3: C1.-, Part5.GND
  N4: S2.Pin_1, S2.Pin_2, 0.D2
  N5: S3.Pin_1, S3.Pin_2, 0.D3
  N6: S4.Pin_1, S4.Pin_2, 0.D4
  N7: LED1.cathode, 0.D7
  N8: LED1.anode, R1.Pin_1
  N9: LED2.cathode, 0.D6
  N10: LED2.anode, R2.Pin_1
  N11: LED3.cathode, 0.D5
  N12: LED3.anode, R3.Pin_1
  N13: 0.D9, Part5.CE
  N14: 0.D10, Part5.CS
  N15: 0.D11/MOSI, Part5.MOSI
  N16: 0.D12/MISO, Part5.MISO
  N17: 0.D13/SCK, Part5.SCK

custom parts:
  18650 battery holder: 18650 Battery
