# Fritzing sketch powerSupplyDemo (saved by Fritzing 0.9.5d)

parts:
  BAT1 = 18650 battery holder [package=battery-18650-kit]
  Part1 = Power Cell LiPo Charger/Booster
  Part2 = Arduino Nano (Rev3.0) (ICSP)
  Part3 = NRF24L01+ Breakout Board
  C1 = Electrolytic Capacitor [capacitance=10μF package="0605 [SMD, electrolytic]"]

nets:
  N1: BAT1.+, Part1.5VIN
  GND: BAT1.-, Part1.GND, Part2.GND, Part3.GND, C1.-
  VCC: Part1.VCC, Part2.5V
  3V3: Part2.3V3, Part3.VCC, C1.+

custom parts:
  18650 battery holder: 18650 Battery
